# Fritzing sketch circit (saved by Fritzing 0.9.3b)
perfboards: 1

parts:
  Mod1 = Raspberry Pi 4B
  U1 = ESP32-38PinWide [part_number=ESP32-38PinWide]
  J1 = Power Jack [package=power_jack_smd]
  Buck_Convertor1 = Buck Convertor [part_number=LM2596 package=THT]
  KY-1 = Keyes Relay [package=THT]  # not connected

nets:
  N1: Mod1.5V, Buck_Convertor1.Positive_Output
  N2: Mod1.GND, Buck_Convertor1.Negative_Output
  N3: Mod1.GPIO14, U1.GPIO3
  N4: Mod1.GPIO15, U1.GPIO1
  N5: J1.PWR, Buck_Convertor1.Positive_Input
  N6: J1.GND, Buck_Convertor1.Negative_Input

notes:
  Pinouts
  =================
  - Led
  - Pneumatic pin relay
  - Motor
  - Ejector 1,2,3,4

custom parts:
  ESP32-38PinWide: Generic 38-Pin ESP32 with wide format (only access to one side of pins on a breadboard) based on Stephen Lilley's HiLetgo ESP-WROOM-32 ESP32 ESP-32S Development Board.
  Buck Convertor: DC to DC buck convertor
  Keyes Relay: The Keyes 5V relay module is suitable for SCM development, home appliance control. It uses a 5V~12V TIL control signal which can control DC / AC signal.
